# Fritzing sketch ExoMy (saved by Fritzing 0.9.4)

parts:
  Part1 = Adafruit 16-Channel PWM + Servo HAT [part_number="Adafruit #2327"]
  U2 = LM2596 step down module
  U1 = LM2596 step down module
  Raspberry_Pi_4 = Raspberry Pi 4 [part_number=RPI-4]  # not connected
  Power_plug = USB-C plug
  U3 = LIPO-2400mAh [package=lipo-2400]
  S2 = Toggle switch
  S1 = Rocker Switch
  SERVO2 = Servo
  SERVO1 = Servo

nets:
  N1: Part1.PWRIN, U2.OUT+
  GND: Part1.GND, U2.IN-, U2.OUT-, U1.IN-, U1.OUT-, Power_plug.GND, S1.pin_4, SERVO2.GND, SERVO1.GND
  N2: Part1.#4, SERVO1.Signal
  +5V: Part1.+5V, SERVO2.+5V, SERVO1.+5V
  N3: Part1.#8, SERVO2.Signal
  N4: U2.IN+, S2.COM
  N5: U1.IN+, S2.L2, S1.pin_2
  N6: U1.OUT+, Power_plug.VCC
  N7: U3.+, S1.pin_1
  N8: U3.-, S1.pin_3

notes:
  Switch 1
  Switch 2
  DC/DC 1
  DC/DC 2
  Motors
  Raspberry Pi
  PWM Board

custom parts:
  Adafruit 16-Channel PWM + Servo HAT: The Raspberry Pi is a wonderful little computer, but one thing it isn't very good at is controlling DC Servo Motors - these motors need very specific and repetitive timing pulses to set the position. Instead of asking the Pi Linux kernel to send these signals, pop on this handy HAT! It adds the capability to control 16 Servos with perfect timing. It can also do PWM up to 1.6 KHz with 12 bit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
  LM2596 step down module: LM2596 DC-DC step down power supply module 3 A.
  USB-C plug: power plug
  LIPO-2400mAh: 2400 mAh 3s Lipo-battery
  Toggle switch: Adapted from: Taiway SP1-T1 SPDT Miniature Toggle Switch.
